// Logisim project ALU.circ as structural Verilog
module _1_Bit_ALU_Version_1 (
  input  a,
  input  Operation,
  input  b,
  output out_4
);

  wire and_1_out, or_1_out;

  and and_1 (and_1_out, a, b);
  _2_1_MUX u_2_1_mux_1 (.In_0(and_1_out), .In_1(or_1_out), .Select(Operation), .Out(out_4));
  or or_1 (or_1_out, a, b);

  // Notes on the sheet:
  //   1-Bit ALU Version 1
  //   Jon Crawford
  //   3/23/2018
endmodule

module _1_Bit_Adder (
  input  Carry_In,
  input  a,
  input  b,
  output Sum,
  output Carry_Out
);

  wire and_1_out, and_2_out, and_3_out, and_4_out, and_5_out, and_6_out, and_7_out, not_1_out, not_2_out,
       not_3_out, not_4_out, not_5_out, not_6_out, not_7_out, not_8_out, not_9_out;

  not not_1 (not_1_out, a);
  not not_2 (not_2_out, b);
  not not_3 (not_3_out, a);
  not not_4 (not_4_out, Carry_In);
  not not_5 (not_5_out, a);
  not not_6 (not_6_out, b);
  not not_7 (not_7_out, Carry_In);
  not not_8 (not_8_out, b);
  not not_9 (not_9_out, Carry_In);
  and and_1 (and_1_out, not_1_out, not_2_out, Carry_In);
  and and_2 (and_2_out, not_3_out, b, not_4_out);
  and and_3 (and_3_out, not_5_out, b, Carry_In);
  and and_4 (and_4_out, a, not_6_out, not_7_out);
  and and_5 (and_5_out, a, not_8_out, Carry_In);
  and and_6 (and_6_out, a, b, not_9_out);
  and and_7 (and_7_out, a, b, Carry_In);
  or or_1 (Carry_Out, and_3_out, and_5_out, and_6_out, and_7_out);
  or or_2 (Sum, and_1_out, and_2_out, and_4_out, and_7_out);

  // Notes on the sheet:
  //   1-Bit Adder
  //   Jon Crawford
  //   3/23/2018
endmodule

module _1_Bit_ALU_Version_2 (
  input  Carry_In,
  input  [1:0] Operation,
  input  a,
  input  b,
  output Result,
  output Carry_Out
);

  wire and_1_out, n1_bit_adder_1_sum, or_1_out;

  and and_1 (and_1_out, a, b);
  or or_1 (or_1_out, a, b);
  _1_Bit_Adder u_1_bit_adder_1 (.a(a), .b(b), .Carry_In(Carry_In), .Carry_Out(Carry_Out), .Sum(n1_bit_adder_1_sum));
  _4_1_MUX u_4_1_mux_1 (
    .In_00(and_1_out), .In_01(or_1_out), .In_10(n1_bit_adder_1_sum), .Sel_0(Operation[1]),
    .Sel_1(Operation[0]), .Out(Result));  // open: In_11

  // Notes on the sheet:
  //   Jon Crawford
  //   2/23/2018
  //   1-Bit ALU Version 2
endmodule

module _1_Bit_ALU_Version_3 (
  input  Ainvert,
  input  Binvert,
  input  Carry_In,
  input  [1:0] Operation,
  input  a,
  input  b,
  input  Less,
  output Result,
  output Carry_Out
);

  wire and_1_out, n1_bit_adder_1_sum, n2_1_mux_1_out, n2_1_mux_2_out, not_1_out, not_2_out, or_1_out;

  _2_1_MUX u_2_1_mux_1 (.In_0(a), .In_1(not_1_out), .Select(Ainvert), .Out(n2_1_mux_1_out));
  not not_1 (not_1_out, a);
  not not_2 (not_2_out, b);
  _2_1_MUX u_2_1_mux_2 (.In_0(b), .In_1(not_2_out), .Select(Binvert), .Out(n2_1_mux_2_out));
  and and_1 (and_1_out, n2_1_mux_1_out, n2_1_mux_2_out);
  or or_1 (or_1_out, n2_1_mux_1_out, n2_1_mux_2_out);
  _1_Bit_Adder u_1_bit_adder_1 (
    .a(n2_1_mux_1_out), .b(n2_1_mux_2_out), .Carry_In(Carry_In), .Carry_Out(Carry_Out),
    .Sum(n1_bit_adder_1_sum));
  _4_1_MUX u_4_1_mux_1 (
    .In_00(and_1_out), .In_01(or_1_out), .In_10(n1_bit_adder_1_sum), .In_11(Less), .Sel_0(Operation[1]),
    .Sel_1(Operation[0]), .Out(Result));

  // Notes on the sheet:
  //   1-Bit ALU Version 3
  //   Jon Crawford
  //   3/23/2018
endmodule

module Top_Bit_ALU (
  input  Ainvert,
  input  Binvert,
  input  Carry_In,
  input  [1:0] Operation,
  input  a,
  input  b,
  input  Less,
  output Result,
  output Set,
  output Overflow
);

  wire and_1_out, n1_bit_adder_1_carry_out, n1_bit_adder_1_sum, n2_1_mux_1_out, n2_1_mux_2_out, not_1_out,
       not_2_out, or_1_out;

  _2_1_MUX u_2_1_mux_1 (.In_0(a), .In_1(not_1_out), .Select(Ainvert), .Out(n2_1_mux_1_out));
  not not_1 (not_1_out, a);
  not not_2 (not_2_out, b);
  _2_1_MUX u_2_1_mux_2 (.In_0(b), .In_1(not_2_out), .Select(Binvert), .Out(n2_1_mux_2_out));
  and and_1 (and_1_out, n2_1_mux_1_out, n2_1_mux_2_out);
  or or_1 (or_1_out, n2_1_mux_1_out, n2_1_mux_2_out);
  _1_Bit_Adder u_1_bit_adder_1 (
    .a(n2_1_mux_1_out), .b(n2_1_mux_2_out), .Carry_In(Carry_In), .Carry_Out(n1_bit_adder_1_carry_out),
    .Sum(n1_bit_adder_1_sum));
  _4_1_MUX u_4_1_mux_1 (
    .In_00(and_1_out), .In_01(or_1_out), .In_10(n1_bit_adder_1_sum), .In_11(Less), .Sel_0(Operation[1]),
    .Sel_1(Operation[0]), .Out(Result));
  xor xor_1 (Set, n1_bit_adder_1_sum, Overflow);
  xor xor_2 (Overflow, n1_bit_adder_1_carry_out, Carry_In);

  // Notes on the sheet:
  //   Top-Bit ALU
  //   Jon Crawford
  //   3/23/2018
endmodule

module _8_Bit_ALU_Version_1 (
  input  Ainvert,
  input  Binvert,
  input  Carry_In,
  input  [1:0] Operation,
  input  [7:0] a,
  input  [7:0] b,
  output [7:0] Result,
  output Overflow
);

  wire n1_bit_alu_version_3_1_carry_out, n1_bit_alu_version_3_2_carry_out, n1_bit_alu_version_3_3_carry_out,
       n1_bit_alu_version_3_4_carry_out, n1_bit_alu_version_3_5_carry_out, n1_bit_alu_version_3_6_carry_out,
       n1_bit_alu_version_3_7_carry_out, top_bit_alu_1_set;

  _1_Bit_ALU_Version_3 u_1_bit_alu_version_3_1 (
    .a(a[0]), .b(b[0]), .Less(top_bit_alu_1_set), .Ainvert(Ainvert), .Binvert(Binvert), .Carry_In(Carry_In),
    .Operation(Operation), .Carry_Out(n1_bit_alu_version_3_1_carry_out), .Result(Result[0]));
  _1_Bit_ALU_Version_3 u_1_bit_alu_version_3_2 (
    .a(a[1]), .b(b[1]), .Less(1'b0), .Ainvert(Ainvert), .Binvert(Binvert),
    .Carry_In(n1_bit_alu_version_3_1_carry_out), .Operation(Operation),
    .Carry_Out(n1_bit_alu_version_3_2_carry_out), .Result(Result[1]));
  _1_Bit_ALU_Version_3 u_1_bit_alu_version_3_3 (
    .a(a[2]), .b(b[2]), .Less(1'b0), .Ainvert(Ainvert), .Binvert(Binvert),
    .Carry_In(n1_bit_alu_version_3_2_carry_out), .Operation(Operation),
    .Carry_Out(n1_bit_alu_version_3_3_carry_out), .Result(Result[2]));
  _1_Bit_ALU_Version_3 u_1_bit_alu_version_3_4 (
    .a(a[3]), .b(b[3]), .Less(1'b0), .Ainvert(Ainvert), .Binvert(Binvert),
    .Carry_In(n1_bit_alu_version_3_3_carry_out), .Operation(Operation),
    .Carry_Out(n1_bit_alu_version_3_4_carry_out), .Result(Result[3]));
  _1_Bit_ALU_Version_3 u_1_bit_alu_version_3_5 (
    .a(a[4]), .b(b[4]), .Less(1'b0), .Ainvert(Ainvert), .Binvert(Binvert),
    .Carry_In(n1_bit_alu_version_3_4_carry_out), .Operation(Operation),
    .Carry_Out(n1_bit_alu_version_3_5_carry_out), .Result(Result[4]));
  _1_Bit_ALU_Version_3 u_1_bit_alu_version_3_6 (
    .a(a[5]), .b(b[5]), .Less(1'b0), .Ainvert(Ainvert), .Binvert(Binvert),
    .Carry_In(n1_bit_alu_version_3_5_carry_out), .Operation(Operation),
    .Carry_Out(n1_bit_alu_version_3_6_carry_out), .Result(Result[5]));
  _1_Bit_ALU_Version_3 u_1_bit_alu_version_3_7 (
    .a(a[6]), .b(b[6]), .Less(1'b0), .Ainvert(Ainvert), .Binvert(Binvert),
    .Carry_In(n1_bit_alu_version_3_6_carry_out), .Operation(Operation),
    .Carry_Out(n1_bit_alu_version_3_7_carry_out), .Result(Result[6]));
  Top_Bit_ALU top_bit_alu_1 (
    .a(a[7]), .b(b[7]), .Less(1'b0), .Ainvert(Ainvert), .Binvert(Binvert),
    .Carry_In(n1_bit_alu_version_3_7_carry_out), .Operation(Operation), .Result(Result[7]),
    .Set(top_bit_alu_1_set), .Overflow(Overflow));

  // Notes on the sheet:
  //   8-Bit ALU Version 1
  //   Jon Crawford
  //   3/23/2018
endmodule

module _8_Bit_ALU_Version_2 (
  input  Anegate,
  input  Bnegate,
  input  [1:0] Operation,
  input  [7:0] a,
  input  [7:0] b,
  output Zero,
  output [7:0] Result,
  output Overflow
);

  wire or_1_out;

  _8_Bit_ALU_Version_1 u_8_bit_alu_version_1_1 (
    .a(a), .b(b), .Ainvert(Anegate), .Binvert(Bnegate), .Carry_In(Bnegate), .Operation(Operation),
    .Result(Result), .Overflow(Overflow));
  or or_1 (or_1_out, Result[0], Result[1], Result[2], Result[3], Result[4], Result[5], Result[6], Result[7]);
  not not_1 (Zero, or_1_out);

  // Notes on the sheet:
  //   8-Bit ALU Version 2
  //   Jon Crawford
  //   3/23/2018
endmodule
