// Logisim project MUX.circ as structural Verilog
module _2_1_MUX (
  input  Select,
  input  In_0,
  input  In_1,
  output Out
);

  wire and_1_out, and_2_out, not_1_out;

  and and_1 (and_1_out, In_0, not_1_out);
  not not_1 (not_1_out, Select);
  and and_2 (and_2_out, In_1, Select);
  or or_1 (Out, and_1_out, and_2_out);

  // Notes on the sheet:
  //   2: 1 MUX
  //   Jon Crawford
  //   3/10/2018
endmodule

module _4_1_MUX (
  input  In_00,
  input  In_01,
  input  In_10,
  input  In_11,
  input  Sel_0,
  input  Sel_1,
  output Out
);

  wire n2_1_mux_2_out, n2_1_mux_3_out;

  _2_1_MUX u_2_1_mux_1 (.In_0(n2_1_mux_2_out), .In_1(n2_1_mux_3_out), .Out(Out));  // open: Select
  _2_1_MUX u_2_1_mux_2 (.In_0(In_00), .In_1(In_01), .Out(n2_1_mux_2_out));  // open: Select
  _2_1_MUX u_2_1_mux_3 (.In_0(In_10), .In_1(In_11), .Out(n2_1_mux_3_out));  // open: Select

  // Notes on the sheet:
  //   4:1 MUX
  //   Jon Crawford
  //   3/10/2018
endmodule
